# Fritzing sketch tupper-turtle (saved by Fritzing 0.7.10b)
breadboards: 1

parts:
  Arduino1 = Arduino
  Part1 = Rotoshield - Motor driver shield for Arduino [part_number="(OR OTHER MOTOR SHEILD)"]
  R1 = Photocell (LDR) [package=THT]
  R2 = Photocell (LDR) [package=THT]
  M1 = DC Motor
  M2 = DC Motor
  M3 = DC Motor
  M4 = DC Motor

nets:
  GND: Arduino1.GND, Part1.GND, R2.pin_1
  N1: Arduino1.D13, Part1.DIG_13
  N2: Arduino1.D12, Part1.DIG_12
  N3: Arduino1.D11, Part1.DIG_11
  N4: Arduino1.D9, Part1.DIG_9
  N5: Arduino1.D8, Part1.DIG_8
  N6: Arduino1.D3, Part1.DIG_3
  N7: Arduino1.+5V, R1.pin_0
  VIN: Arduino1.VIN, Part1.VIN
  N8: Arduino1.A5, R1.pin_1, R2.pin_0
  N9: Part1.M1-2, M1.pin_2, M4.pin_2
  N10: Part1.M1-1, M1.pin_1, M4.pin_1
  N11: Part1.M2-2, M2.pin_2, M3.pin_2
  N12: Part1.M2-1, M2.pin_1, M3.pin_1

notes:
  Right Motor(s)
  Left Motor(s)
  Blue wires are usually uncecessary for motor sheilds because the ardiuno and shield plug into each other. Pins are set for an Arduino brand motor sheild, not the Rotoshield pictured. If you are using another sheild, double check the pin configurations for that shield and update the source code if necessary. https://github.com/new-paltz-robotics/tupper-turtle
